# Fritzing sketch wariometr (saved by Fritzing 0.7.0b)
breadboards: 1

parts:
  LCD1 = LCD screen
  Part1 = Barometric Pressure Sensor - BMP085 Breakout
  Arduino1 = Arduino
  R1 = Trimmer Potentiometer [maximum_resistance=10kΩ package=THT]
  S1 = Pushbutton [package="[THT]"]
  S2 = Pushbutton [package="[THT]"]
  R2 = Resistor [tolerance=±5% resistance=220 package=THT]
  Part2 = Bluetooth Mate Silver
  R3 = Resistor [tolerance=±5% resistance=220 package=THT]  # not connected
  Q1 = NPN-Transistor [package="TO92 [THT]"]
  R4 = Resistor [tolerance=±5% resistance=220 package=THT]  # not connected

nets (from the breadboard view):
  GND: LCD1.VSS, LCD1.R/W, LCD1.LED-, Part1.GND, Arduino1.GND, R1.leg1, R2.Pin_0, Part2.GND
  VDD: LCD1.VDD, Arduino1.+5V, R1.leg2, S1.Pin_1, S1.Pin_2, S2.Pin_3, S2.Pin_4, Q1.E
  N1: LCD1.V0, R1.wiper
  N2: LCD1.RS, Arduino1.D12
  N3: LCD1.E, Arduino1.D11
  N4: LCD1.DB4, Arduino1.D10
  N5: LCD1.DB5, Arduino1.D9
  N6: LCD1.DB6, Arduino1.D8
  N7: LCD1.DB7, Arduino1.D7
  VCC: Part1.VCC, Arduino1.3V3, Part2.RTS_5V
  N8: Part1.SCL, Arduino1.A5
  N9: Part1.SDA, Arduino1.A4
  N10: Arduino1.D3, Arduino1.D2, S1.Pin_3, S1.Pin_4, S2.Pin_1, S2.Pin_2, R2.Pin_1
  N11: Arduino1.D1TX, Part2.RX_5V
  N12: Arduino1.D0RX, Part2.TX_5V
